# Fritzing sketch MIDi_To_Fan_layout (saved by Fritzing 0.6.3b)
breadboards: 1

parts:
  Arduino1 = Arduino
  DIN1 = DIN-5 jack (MIDI) [package=THT]
  R1 = Resistor [tolerance=±5% resistance=220 package=THT]
  D1 = Rectifier Diode [part_number=1N4001 package="300 mil [THT]"]
  R2 = Resistor [tolerance=±5% resistance=270 package=THT]
  IC1 = IC, DIP package, 8 pins [chip_label="6N 138 " spacing=300mil]
  Q2 = PNP-Transistor [package="TO92 [THT]"]
  Q1 = PNP-Transistor [package="TO92 [THT]"]
  SPKR1 = Loudspeaker
  VCC1 = Battery block 9V
  SPKR2 = Loudspeaker

nets:
  GND: Arduino1.GND, IC1.pin5, IC1.pin7, Q2.C, Q1.C, VCC1.-
  N1: Arduino1.D8, Q2.B
  N2: Arduino1.D4, Q1.B
  N3: Arduino1.D0RX, R2.Pin_1, IC1.pin6
  N4: DIN1.5, D1.cathode, IC1.pin2
  N5: DIN1.4, R1.Pin_1
  N6: R1.Pin_0, D1.anode, IC1.pin3
  N7: R2.Pin_0, IC1.pin8
  N8: Q2.E, SPKR1.pin1
  N9: Q1.E, SPKR2.pin1
  N10: SPKR1.pin2, VCC1.+, SPKR2.pin2
